// Logisim project IFT 211 Smart Water Tank Monitoring & Control System.circ as structural Verilog: 1 circuit, main circuit main
module main (
  input  S0,
  input  S1,
  input  S2,
  input  S3,
  input  CLOCK,
  input  RESET,
  output LEVEL1,
  output LEVEL0,
  output FULL,
  output PUMP,
  output VALID,
  output STORED_MSB,
  output STORED_LSB,
  output ALARM,
  output SEG_A,
  output SEG_B,
  output SEG_C,
  output SEG_D,
  output SEG_E,
  output SEG_F,
  output SEG_G
);

  wire AD0, AD1, ANY, CD0, CD1, CEN, FN, HL, HM, INV, LD0, LD1, LL, LM, LMN, MA, MB, MULTI, NL, NM, NOM, P0,
       P1, P2, P3, P4, P5, Q0, Q0N, Q1, RN, VF;

  or or_1 (LEVEL1, S2, S3);
  or or_2 (LEVEL0, S1, S3);
  not not_1 (RN, RESET);
  and and_1 (VF, VALID, FULL);
  and and_2 (P0, S0, S1);
  and and_3 (P1, S0, S2);
  and and_4 (P2, S0, S3);
  and and_5 (P3, S1, S2);
  and and_6 (P4, S1, S3);
  and and_7 (P5, S2, S3);
  and and_8 (LM, VALID, LEVEL1);
  and and_9 (HM, INV, SEG_G);
  and and_10 (LL, VALID, LEVEL0);
  and and_11 (HL, INV, STORED_LSB);
  and and_12 (FULL, LEVEL1, LEVEL0);
  or or_3 (NM, LM, HM);
  or or_4 (NL, LL, HL);
  or or_5 (MA, P0, P1, P2);
  or or_6 (MB, P3, P4, P5);
  or or_7 (ANY, S0, S1, S2, S3);
  not not_2 (FN, FULL);
  and and_13 (LD1, RN, NM);
  and and_14 (LD0, RN, NL);
  or or_8 (MULTI, MA, MB);
  and and_15 (PUMP, VALID, FN);
  D_Flip_Flop d_ff_1 (.D(LD1), .clk(CLOCK), .Q(SEG_G));  // open: Qn, preset, reset
  D_Flip_Flop d_ff_2 (.D(LD0), .clk(CLOCK), .Q(STORED_LSB));  // open: Qn, preset, reset
  not not_3 (NOM, MULTI);
  and and_16 (CEN, VF, RN);
  or or_9 (AD1, Q1, Q0);
  not not_4 (Q0N, Q0);
  not not_5 (LMN, SEG_G);
  not not_6 (SEG_E, STORED_LSB);
  and and_17 (VALID, ANY, NOM);
  or or_10 (AD0, Q1, Q0N);
  or or_11 (SEG_A, SEG_G, SEG_E);
  or or_12 (SEG_C, LMN, STORED_LSB);
  or or_13 (SEG_D, SEG_G, SEG_E);
  and and_18 (SEG_F, LMN, SEG_E);
  not not_7 (INV, VALID);
  and and_19 (CD1, CEN, AD1);
  and and_20 (CD0, CEN, AD0);
  D_Flip_Flop d_ff_3 (.D(CD1), .clk(CLOCK), .Q(Q1));  // open: Qn, preset, reset
  D_Flip_Flop d_ff_4 (.D(CD0), .clk(CLOCK), .Q(Q0));  // open: Qn, preset, reset
  and and_21 (ALARM, Q1, Q0);
  _7_Segment_Display u_7_segment_display_1 (
    .g(SEG_G), .f(SEG_F), .a(SEG_A), .b(1'b1), .e(SEG_E), .d(SEG_D), .c(SEG_C));  // open: dp

  assign SEG_B = 1'b1;
  assign STORED_MSB = SEG_G;
  // also tied to VCC on the sheet: SEG_A

  // Other names for the same wires on the sheet: L0R = LEVEL0; L1R = LEVEL1; LQ = STORED_LSB; LQN = SEG_E; MQ = SEG_G;
  //   SA = SEG_A; SC = SEG_C; SD = SEG_D; SF = SEG_F

  // Notes on the sheet:
  //   ENCODER / PUMP
  //   LEVEL REGISTER
  //   SEVEN-SEGMENT DECODER
  //   FULL-TIMEOUT COUNTER / ALARM
endmodule
